// Logisim project ddca 8 to 3.circ as structural Verilog: 1 circuit, main circuit main
module main (
  input  in_1,
  input  in_2,
  input  in_3,
  input  in_4,
  input  in_5,
  input  in_6,
  input  in_7,
  input  in_8,
  output out_9,
  output out_10,
  output out_11,
  output out_12
);

  wire and_1_out, and_2_out, and_3_out, and_4_out, and_5_out, and_6_out, and_7_out, not_1_out, not_2_out;

  not not_1 (not_1_out, in_1);
  not not_2 (not_2_out, in_2);
  not not_3 (not_2_out, in_3);
  not not_4 (not_2_out, in_4);
  // NOT_Gate not_5 has open pins: in=in_5, out=open
  // NOT_Gate not_6 has open pins: in=in_6, out=open
  // NOT_Gate not_7 has open pins: in=in_7, out=open
  not not_8 (not_2_out, in_8);
  and and_1 (and_1_out, not_2_out, in_1);
  and and_2 (and_2_out, not_1_out, not_2_out, in_2, not_2_out);
  and and_3 (and_3_out, not_2_out, in_3, not_2_out);
  and and_4 (and_4_out, in_4, not_2_out, not_2_out);
  and and_5 (and_5_out, in_5, not_2_out, not_2_out, not_2_out);
  and and_6 (and_6_out, in_6, not_2_out, not_2_out, not_2_out);
  and and_7 (and_7_out, in_7, not_2_out, not_2_out, not_2_out);
  and and_8 (and_6_out, in_8, not_2_out, not_2_out, not_2_out);
  or or_1 (out_9, and_1_out, and_2_out);
  or or_2 (out_10, and_3_out, and_5_out);
  or or_3 (out_11, and_4_out, and_4_out, and_7_out);
  or or_4 (out_12, and_6_out, not_2_out);
endmodule
