// Logisim project ddca project main.circ as structural Verilog: 1 circuit, main circuit main
module main (
  input  L,
  input  H,
  input  PUMP_MOTOR_M,
  input  OF,
  input  BUZZER_B
);

  wire AND_out, NOT_2_out, NOT_out;

  not NOT (NOT_out, L);
  not NOT_2 (NOT_2_out, H);
  and AND (AND_out, NOT_2_out, OF);
  LED LED (.in(NOT_out));
  LED FAULT_F (.in(AND_out));
endmodule
